// Logisim project logi7400dip.circ as structural Verilog: 60 circuits, main circuit README
module README (
  input  in_1
);

  wire dip_74148_1_a0, dip_74148_1_a1, dip_74148_1_a2, dip_74148_1_eo, dip_74148_1_gs, dipswitch_1_sw1,
       dipswitch_1_sw2, dipswitch_1_sw3, dipswitch_1_sw4, dipswitch_1_sw5, dipswitch_1_sw6, dipswitch_1_sw7,
       dipswitch_1_sw8;

  DipSwitch dipswitch_1 (
    .sw1(dipswitch_1_sw1), .sw2(dipswitch_1_sw2), .sw3(dipswitch_1_sw3), .sw4(dipswitch_1_sw4),
    .sw5(dipswitch_1_sw5), .sw6(dipswitch_1_sw6), .sw7(dipswitch_1_sw7), .sw8(dipswitch_1_sw8));
  DIP_74148 dip_74148_1 (
    .D1(dipswitch_1_sw7), .D0(dipswitch_1_sw8), .D2(dipswitch_1_sw6), .D3(dipswitch_1_sw5),
    .D4(dipswitch_1_sw4), .D5(dipswitch_1_sw3), .D6(dipswitch_1_sw2), .D7(dipswitch_1_sw1), .EI(in_1),
    .GS(dip_74148_1_gs), .A0(dip_74148_1_a0), .A1(dip_74148_1_a1), .EO(dip_74148_1_eo), .A2(dip_74148_1_a2));
  LedBar #(.matrixcols(3)) ledbar_1 (.led0(dip_74148_1_a2), .led1(dip_74148_1_a1), .led2(dip_74148_1_a0));
  LedBar #(.matrixcols(2)) ledbar_2 (.led0(dip_74148_1_gs), .led1(dip_74148_1_eo));

  // Notes on the sheet:
  //   Logisim 7400 series integrated circuits library
  //   Copyright (C) 2015 - 2016 by Stefan Rothe
  //   This library is licenced under the GNU Lesser General Public Licence version 3.
endmodule

// 7400
module DIP_7400 (
  input  A1,
  input  B1,
  input  A2,
  input  B2,
  input  A3,
  input  B3,
  input  A4,
  input  B4,
  output Y1,
  output Y2,
  output Y3,
  output Y4
);

  nand nand_1 (Y1, A1, B1);
  nand nand_2 (Y2, A2, B2);
  nand nand_3 (Y3, A3, B3);
  nand nand_4 (Y4, A4, B4);
endmodule

// 7402
module DIP_7402 (
  input  A1,
  input  B1,
  input  A2,
  input  B2,
  input  A3,
  input  B3,
  input  A4,
  input  B4,
  output Y1,
  output Y2,
  output Y3,
  output Y4
);

  nor nor_1 (Y1, A1, B1);
  nor nor_2 (Y2, A2, B2);
  nor nor_3 (Y3, A3, B3);
  nor nor_4 (Y4, A4, B4);
endmodule

// 7403
module DIP_7403 (
  input  A1,
  input  B1,
  input  A2,
  input  B2,
  input  A3,
  input  B3,
  input  A4,
  input  B4,
  output Y1,
  output Y2,
  output Y3,
  output Y4
);

  wire and_1_out, and_2_out, and_3_out, and_4_out;

  and and_1 (and_1_out, A1, B1);
  and and_2 (and_2_out, A2, B2);
  and and_3 (and_3_out, A3, B3);
  and and_4 (and_4_out, A4, B4);
  assign Y1 = and_1_out ? 1'b0 : 1'bz;  // Controlled_Buffer controlled_buffer_1
  assign Y2 = and_2_out ? 1'b0 : 1'bz;  // Controlled_Buffer controlled_buffer_2
  assign Y3 = and_3_out ? 1'b0 : 1'bz;  // Controlled_Buffer controlled_buffer_3
  assign Y4 = and_4_out ? 1'b0 : 1'bz;  // Controlled_Buffer controlled_buffer_4
endmodule

// 7404
module DIP_7404 (
  input  A1,
  input  A2,
  input  A3,
  input  A4,
  input  A5,
  input  A6,
  output Y1,
  output Y2,
  output Y3,
  output Y4,
  output Y5,
  output Y6
);

  not not_1 (Y1, A1);
  not not_2 (Y2, A2);
  not not_3 (Y3, A3);
  not not_4 (Y4, A4);
  not not_5 (Y5, A5);
  not not_6 (Y6, A6);
endmodule

// 7405
module DIP_7405 (
  input  A1,
  input  A2,
  input  A3,
  input  A4,
  input  A5,
  input  A6,
  output Y1,
  output Y2,
  output Y3,
  output Y4,
  output Y5,
  output Y6
);

  assign Y1 = A1 ? 1'b0 : 1'bz;  // Controlled_Buffer controlled_buffer_1
  assign Y2 = A2 ? 1'b0 : 1'bz;  // Controlled_Buffer controlled_buffer_2
  assign Y3 = A3 ? 1'b0 : 1'bz;  // Controlled_Buffer controlled_buffer_3
  assign Y4 = A4 ? 1'b0 : 1'bz;  // Controlled_Buffer controlled_buffer_4
  assign Y5 = A5 ? 1'b0 : 1'bz;  // Controlled_Buffer controlled_buffer_5
  assign Y6 = A6 ? 1'b0 : 1'bz;  // Controlled_Buffer controlled_buffer_6
endmodule

// 7408
module DIP_7408 (
  input  A1,
  input  B1,
  input  A2,
  input  B2,
  input  A3,
  input  B3,
  input  A4,
  input  B4,
  output Y1,
  output Y2,
  output Y3,
  output Y4
);

  and and_1 (Y1, A1, B1);
  and and_2 (Y2, A2, B2);
  and and_3 (Y3, A3, B3);
  and and_4 (Y4, A4, B4);
endmodule

// 7410
module DIP_7410 (
  input  A1,
  input  B1,
  input  C1,
  input  A2,
  input  B2,
  input  C2,
  input  A3,
  input  B3,
  input  C3,
  output Y1,
  output Y2,
  output Y3
);

  nand nand_1 (Y1, A1, B1, C1);
  nand nand_2 (Y2, A2, B2, C2);
  nand nand_3 (Y3, A3, B3, C3);
endmodule

// 7411
module DIP_7411 (
  input  A1,
  input  B1,
  input  C1,
  input  A2,
  input  B2,
  input  C2,
  input  A3,
  input  B3,
  input  C3,
  output Y1,
  output Y2,
  output Y3
);

  and and_1 (Y1, A1, B1, C1);
  and and_2 (Y2, A2, B2, C2);
  and and_3 (Y3, A3, B3, C3);
endmodule

// 7413
module DIP_7413 (
  input  A1,
  input  B1,
  input  C1,
  input  D1,
  input  A2,
  input  B2,
  input  C2,
  input  D2,
  output Y1,
  output Y2
);

  nand nand_1 (Y1, A1, B1, C1, D1);
  nand nand_2 (Y2, A2, B2, C2, D2);
endmodule

// 7414
module DIP_7414 (
  input  A1,
  input  A2,
  input  A3,
  input  A4,
  input  A5,
  input  A6,
  output Y1,
  output Y2,
  output Y3,
  output Y4,
  output Y5,
  output Y6
);

  not not_1 (Y1, A1);
  not not_2 (Y2, A2);
  not not_3 (Y3, A3);
  not not_4 (Y4, A4);
  not not_5 (Y5, A5);
  not not_6 (Y6, A6);
endmodule

// 7420
module DIP_7420 (
  input  A1,
  input  B1,
  input  C1,
  input  D1,
  input  A2,
  input  B2,
  input  C2,
  input  D2,
  output Y1,
  output Y2
);

  nand nand_1 (Y1, A1, B1, C1, D1);
  nand nand_2 (Y2, A2, B2, C2, D2);
endmodule

// 7421
module DIP_7421 (
  input  A1,
  input  B1,
  input  C1,
  input  D1,
  input  A2,
  input  B2,
  input  C2,
  input  D2,
  output Y1,
  output Y2
);

  and and_1 (Y1, A1, B1, C1, D1);
  and and_2 (Y2, A2, B2, C2, D2);
endmodule

// 7425
module DIP_7425 (
  input  A1,
  input  B1,
  input  C1,
  input  D1,
  input  A2,
  input  B2,
  input  C2,
  input  D2,
  output Y1,
  output Y2
);

  nor nor_1 (Y1, A1, B1, C1, D1);
  nor nor_2 (Y2, A2, B2, C2, D2);
endmodule

// 7427
module DIP_7427 (
  input  A1,
  input  B1,
  input  C1,
  input  A2,
  input  B2,
  input  C2,
  input  A3,
  input  B3,
  input  C3,
  output Y1,
  output Y2,
  output Y3
);

  nor nor_1 (Y1, A1, B1, C1);
  nor nor_2 (Y2, A2, B2, C2);
  nor nor_3 (Y3, A3, B3, C3);
endmodule

// 7430
module DIP_7430 (
  input  A,
  input  B,
  input  C,
  input  D,
  input  E,
  input  F,
  input  G,
  input  H,
  output Y
);

  nand nand_1 (Y, A, B, C, D, E, F, G, H);
endmodule

// 7432
module DIP_7432 (
  input  A1,
  input  B1,
  input  A2,
  input  B2,
  input  A3,
  input  B3,
  input  A4,
  input  B4,
  output Y1,
  output Y2,
  output Y3,
  output Y4
);

  or or_1 (Y1, A1, B1);
  or or_2 (Y2, A2, B2);
  or or_3 (Y3, A3, B3);
  or or_4 (Y4, A4, B4);
endmodule

// 7442
module DIP_7442 (
  input  D1,
  input  D2,
  input  D3,
  input  D4,
  output Y0,
  output Y1,
  output Y2,
  output Y3,
  output Y4,
  output Y5,
  output Y6,
  output Y7,
  output Y8,
  output Y9
);

  wire nand_1_out, nand_2_out, nand_3_out, nand_4_out, nand_5_out, nand_6_out, nand_7_out, not_1_out,
       not_2_out, not_3_out, not_4_out, not_5_out, not_6_out, not_7_out, not_8_out;

  not not_1 (not_1_out, D1);
  not not_2 (not_2_out, D2);
  not not_3 (not_3_out, D3);
  not not_4 (not_4_out, D4);
  not not_5 (not_5_out, not_1_out);
  not not_6 (not_6_out, not_2_out);
  not not_7 (not_7_out, not_3_out);
  not not_8 (not_8_out, not_4_out);
  nand nand_1 (nand_1_out, not_1_out, not_2_out);
  nand nand_2 (nand_2_out, not_5_out, not_2_out);
  nand nand_3 (nand_3_out, not_1_out, not_6_out);
  nand nand_4 (nand_4_out, not_5_out, not_6_out);
  nand nand_5 (nand_5_out, not_3_out, not_4_out);
  nand nand_6 (nand_6_out, not_7_out, not_4_out);
  nand nand_7 (nand_7_out, not_3_out, not_8_out);
  nand nand_8 (Y0, ~nand_1_out, ~nand_5_out);  // NAND_Gate
  nand nand_9 (Y1, ~nand_2_out, ~nand_5_out);  // NAND_Gate
  nand nand_10 (Y2, ~nand_3_out, ~nand_5_out);  // NAND_Gate
  nand nand_11 (Y3, ~nand_4_out, ~nand_5_out);  // NAND_Gate
  nand nand_12 (Y4, ~nand_1_out, ~nand_6_out);  // NAND_Gate
  nand nand_13 (Y5, ~nand_2_out, ~nand_6_out);  // NAND_Gate
  nand nand_14 (Y6, ~nand_3_out, ~nand_6_out);  // NAND_Gate
  nand nand_15 (Y7, ~nand_4_out, ~nand_6_out);  // NAND_Gate
  nand nand_16 (Y8, ~nand_1_out, ~nand_7_out);  // NAND_Gate
  nand nand_17 (Y9, ~nand_2_out, ~nand_7_out);  // NAND_Gate
endmodule

module DIP_7447 (
  input  D1,
  input  D2,
  input  D3,
  input  D4,
  input  BI_RBO,
  input  LT,
  input  RBI,
  output a,
  output b,
  output c,
  output d,
  output e,
  output f,
  output g
);

  wire and_1_out, and_2_out, and_3_out, and_4_out, and_5_out, and_6_out, and_7_out, and_8_out, and_9_out,
       and_10_out, and_11_out, and_12_out, and_13_out, and_14_out, and_15_out, and_16_out, and_17_out,
       buffer_1_out, buffer_2_out, nand_1_out, nand_2_out, nand_3_out, nand_4_out, nand_5_out, nand_6_out,
       nand_7_out, nand_8_out, not_1_out, not_2_out, not_3_out, or_1_out, or_2_out, or_3_out, or_4_out,
       or_5_out, or_6_out, or_7_out, pull_resistor_1_node;

  nand nand_1 (nand_1_out, D1, buffer_1_out);
  nand nand_2 (nand_2_out, D2, buffer_1_out);
  nand nand_3 (nand_3_out, D3, buffer_1_out);
  not not_1 (not_1_out, D4);
  Pull_Resistor pull_resistor_1 (.node(pull_resistor_1_node));
  Transistor transistor_1 (.in(nand_4_out), .out(pull_resistor_1_node), .gate(not_2_out));
  not not_2 (not_2_out, BI_RBO);
  nand nand_4 (nand_4_out, buffer_1_out, not_3_out, not_1_out, nand_3_out, nand_2_out, nand_1_out);
  buf buffer_1 (buffer_1_out, LT);
  not not_3 (not_3_out, RBI);
  nand nand_5 (nand_5_out, nand_1_out, pull_resistor_1_node);
  nand nand_6 (nand_6_out, nand_2_out, pull_resistor_1_node);
  nand nand_7 (nand_7_out, nand_3_out, pull_resistor_1_node);
  nand nand_8 (nand_8_out, not_1_out, pull_resistor_1_node);
  and and_1 (and_1_out, nand_6_out, nand_8_out);
  and and_2 (and_2_out, nand_1_out, nand_7_out);
  and and_3 (and_3_out, nand_5_out, nand_2_out, nand_3_out, not_1_out);
  and and_4 (and_4_out, nand_6_out, nand_8_out);
  and and_5 (and_5_out, nand_5_out, nand_2_out, nand_7_out);
  and and_6 (and_6_out, nand_1_out, nand_6_out, nand_7_out);
  and and_7 (and_7_out, nand_7_out, nand_8_out);
  and and_8 (and_8_out, nand_1_out, nand_6_out, nand_3_out);
  and and_9 (and_9_out, nand_5_out, nand_2_out, nand_3_out);
  and and_10 (and_10_out, nand_1_out, nand_2_out, nand_7_out);
  and and_11 (and_11_out, nand_5_out, nand_6_out, nand_7_out);
  buf buffer_2 (buffer_2_out, nand_5_out);
  and and_12 (and_12_out, nand_2_out, nand_7_out);
  and and_13 (and_13_out, nand_5_out, nand_6_out);
  and and_14 (and_14_out, nand_6_out, nand_3_out);
  and and_15 (and_15_out, nand_5_out, nand_3_out, not_1_out);
  and and_16 (and_16_out, nand_5_out, nand_6_out, nand_7_out);
  and and_17 (and_17_out, nand_2_out, nand_3_out, not_1_out, buffer_1_out);
  or or_1 (or_1_out, and_1_out, and_2_out, and_3_out);
  or or_2 (or_2_out, and_4_out, and_5_out, and_6_out);
  or or_3 (or_3_out, and_7_out, and_8_out);
  or or_4 (or_4_out, and_9_out, and_10_out, and_11_out);
  or or_5 (or_5_out, buffer_2_out, and_12_out);
  or or_6 (or_6_out, and_13_out, and_14_out, and_15_out);
  or or_7 (or_7_out, and_16_out, and_17_out);
  Transistor #(.\type ("n")) transistor_2 (.in(1'b0), .out(a), .gate(or_1_out));
  Transistor #(.\type ("n")) transistor_3 (.in(1'b0), .out(b), .gate(or_2_out));
  Transistor #(.\type ("n")) transistor_4 (.in(1'b0), .out(c), .gate(or_3_out));
  Transistor #(.\type ("n")) transistor_5 (.in(1'b0), .out(d), .gate(or_4_out));
  Transistor #(.\type ("n")) transistor_6 (.in(1'b0), .out(e), .gate(or_5_out));
  Transistor #(.\type ("n")) transistor_7 (.in(1'b0), .out(f), .gate(or_6_out));
  Transistor #(.\type ("n")) transistor_8 (.in(1'b0), .out(g), .gate(or_7_out));

  // Notes on the sheet:
  //   b: pull=down
  //   c: pull=down
  //   d: pull=down
  //   e: pull=down
  //   a: pull=down
  //   f: pull=down
  //   g: pull=down
endmodule

// 7451
module DIP_7451 (
  input  A1,
  input  B1,
  input  C1,
  input  D1,
  input  E1,
  input  F1,
  input  A2,
  input  B2,
  input  C2,
  input  D2,
  output Y1,
  output Y2
);

  wire and_1_out, and_2_out, and_3_out, and_4_out;

  and and_1 (and_1_out, A1, B1, C1);
  and and_2 (and_2_out, D1, E1, F1);
  and and_3 (and_3_out, A2, B2);
  and and_4 (and_4_out, C2, D2);
  nor nor_1 (Y1, and_1_out, and_2_out);
  nor nor_2 (Y2, and_3_out, and_4_out);
endmodule

module DIP_7473 (
  input  J1,
  input  CLK1,
  input  K1,
  input  CLR1,
  input  J2,
  input  CLK2,
  input  K2,
  input  CLR2,
  output Q1,
  output R1,
  output Q2,
  output R2
);

  wire not_1_out, not_2_out, not_3_out, not_4_out;

  not not_1 (not_1_out, CLK1);
  not not_2 (not_2_out, CLR1);
  not not_3 (not_3_out, CLK2);
  not not_4 (not_4_out, CLR2);
  JK_Flip_Flop jk_flip_flop_1 (.CLR(not_2_out), .SET(1'b0), .CLK(not_1_out), .K(K1), .J(J1), .R(R1), .Q(Q1));
  JK_Flip_Flop jk_flip_flop_2 (.CLR(not_4_out), .SET(1'b0), .CLK(not_3_out), .K(K2), .J(J2), .R(R2), .Q(Q2));
endmodule

// 7474
module DIP_7474 (
  input  SET1,
  input  D1,
  input  CLK1,
  input  CLR1,
  input  SET2,
  input  D2,
  input  CLK2,
  input  CLR2,
  output Q1,
  output R1,
  output Q2,
  output R2
);

  wire not_1_out, not_2_out, not_3_out, not_4_out;

  not not_1 (not_1_out, SET1);
  D_Flip_Flop d_flip_flop_1 (.SET(not_1_out), .CLR(not_2_out), .D(D1), .CLK(CLK1), .Q(Q1), .R(R1));
  not not_2 (not_2_out, CLR1);
  not not_3 (not_3_out, SET2);
  D_Flip_Flop d_flip_flop_2 (.SET(not_3_out), .CLR(not_4_out), .D(D2), .CLK(CLK2), .Q(Q2), .R(R2));
  not not_4 (not_4_out, CLR2);
endmodule

// 7476
module DIP_7476 (
  input  SET1,
  input  J1,
  input  CLK1,
  input  K1,
  input  CLR1,
  input  SET2,
  input  J2,
  input  CLK2,
  input  K2,
  input  CLR2,
  output Q1,
  output R1,
  output Q2,
  output R2
);

  wire not_1_out, not_2_out, not_3_out, not_4_out, not_5_out, not_6_out;

  not not_1 (not_1_out, SET1);
  not not_2 (not_2_out, CLK1);
  not not_3 (not_3_out, CLR1);
  not not_4 (not_4_out, SET2);
  not not_5 (not_5_out, CLK2);
  not not_6 (not_6_out, CLR2);
  JK_Flip_Flop jk_flip_flop_1 (.CLR(not_3_out), .SET(not_1_out), .CLK(not_2_out), .K(K1), .J(J1), .R(R1), .Q(Q1));
  JK_Flip_Flop jk_flip_flop_2 (.CLR(not_6_out), .SET(not_4_out), .CLK(not_5_out), .K(K2), .J(J2), .R(R2), .Q(Q2));
endmodule

// 7483
module DIP_7483 (
  input  CIN,
  input  A1,
  input  B1,
  input  A2,
  input  B2,
  input  A3,
  input  B3,
  input  A4,
  input  B4,
  output Y1,
  output Y2,
  output Y3,
  output Y4,
  output COUT
);

  wire and_1_out, and_2_out, and_3_out, and_4_out, and_5_out, and_6_out, and_7_out, and_8_out, and_9_out,
       and_10_out, and_11_out, and_12_out, and_13_out, and_14_out, nand_1_out, nand_2_out, nand_3_out,
       nand_4_out, nor_1_out, nor_2_out, nor_3_out, nor_4_out, nor_5_out, nor_6_out, nor_7_out, not_1_out,
       not_2_out, not_3_out, not_4_out, not_5_out, not_6_out;

  not not_1 (not_1_out, CIN);
  nor nor_1 (nor_1_out, A1, B1);
  nand nand_1 (nand_1_out, A1, B1);
  nor nor_2 (nor_2_out, A2, B2);
  nand nand_2 (nand_2_out, A2, B2);
  nor nor_3 (nor_3_out, A3, B3);
  nand nand_3 (nand_3_out, A3, B3);
  nor nor_4 (nor_4_out, A4, B4);
  nand nand_4 (nand_4_out, A4, B4);
  not not_2 (not_2_out, not_1_out);
  not not_3 (not_3_out, nor_1_out);
  and and_1 (and_1_out, not_1_out, nand_1_out);
  not not_4 (not_4_out, nor_2_out);
  and and_2 (and_2_out, not_1_out, nand_1_out, nand_2_out);
  and and_3 (and_3_out, nand_2_out, nor_1_out);
  not not_5 (not_5_out, nor_3_out);
  and and_4 (and_4_out, not_1_out, nand_1_out, nand_2_out, nand_3_out);
  and and_5 (and_5_out, nand_2_out, nand_3_out, nor_1_out);
  and and_6 (and_6_out, nand_3_out, nor_2_out);
  not not_6 (not_6_out, nor_4_out);
  and and_7 (and_7_out, nand_1_out, nand_3_out);
  and and_8 (and_8_out, nand_2_out, nand_3_out, nand_4_out, nor_1_out);
  and and_9 (and_9_out, nand_3_out, nand_4_out, nor_2_out);
  and and_10 (and_10_out, nand_4_out, nor_3_out);
  and and_11 (and_11_out, not_3_out, nand_1_out);
  nor nor_5 (nor_5_out, and_1_out, nor_1_out);
  and and_12 (and_12_out, not_4_out, nand_2_out);
  nor nor_6 (nor_6_out, and_2_out, and_3_out, nor_2_out);
  and and_13 (and_13_out, not_5_out, nand_3_out);
  nor nor_7 (nor_7_out, and_4_out, and_5_out, and_6_out, nor_3_out);
  and and_14 (and_14_out, not_6_out, nand_4_out);
  nor nor_8 (COUT, and_7_out, and_8_out, and_9_out, and_10_out, nor_4_out);
  xor xor_1 (Y1, not_2_out, and_11_out);
  xor xor_2 (Y2, nor_5_out, and_12_out);
  xor xor_3 (Y3, nor_6_out, and_13_out);
  xor xor_4 (Y4, nor_7_out, and_14_out);
endmodule

// 7485
module DIP_7485 (
  input  A4,
  input  B4,
  input  A3,
  input  B3,
  input  CLT,
  input  CEQ,
  input  CGT,
  input  A2,
  input  B2,
  input  A1,
  input  B1,
  output YGT,
  output YEQ,
  output YLT
);

  wire and_1_out, and_2_out, and_3_out, and_4_out, and_5_out, and_6_out, and_7_out, and_8_out, and_9_out,
       and_10_out, and_11_out, and_12_out, and_13_out, and_14_out, and_16_out, and_17_out, and_18_out,
       and_19_out, and_20_out, and_21_out, nand_1_out, nand_2_out, nand_3_out, nand_4_out, nor_1_out,
       nor_2_out, nor_3_out, nor_4_out;

  nand nand_1 (nand_1_out, A4, B4);
  nand nand_2 (nand_2_out, A3, B3);
  nand nand_3 (nand_3_out, A2, B2);
  nand nand_4 (nand_4_out, A1, B1);
  and and_1 (and_1_out, A4, nand_1_out);
  and and_2 (and_2_out, nand_1_out, B4);
  and and_3 (and_3_out, A3, nand_2_out);
  and and_4 (and_4_out, nand_2_out, B3);
  and and_5 (and_5_out, A2, nand_3_out);
  and and_6 (and_6_out, nand_3_out, B2);
  and and_7 (and_7_out, A1, nand_4_out);
  and and_8 (and_8_out, nand_4_out, B1);
  nor nor_1 (nor_1_out, and_1_out, and_2_out);
  nor nor_2 (nor_2_out, and_3_out, and_4_out);
  nor nor_3 (nor_3_out, and_5_out, and_6_out);
  nor nor_4 (nor_4_out, and_7_out, and_8_out);
  and and_9 (and_9_out, B4, nand_1_out);
  and and_10 (and_10_out, B3, nand_2_out, nor_1_out);
  and and_11 (and_11_out, B2, nand_3_out, nor_1_out, nor_2_out);
  and and_12 (and_12_out, nand_4_out, nor_2_out);
  and and_13 (and_13_out, nor_2_out, nor_4_out);
  and and_14 (and_14_out, nor_2_out, nor_4_out);
  and and_15 (YEQ, nor_2_out, nor_3_out);
  and and_16 (and_16_out, nor_4_out, nor_2_out);
  and and_17 (and_17_out, nor_4_out, nor_2_out);
  and and_18 (and_18_out, nor_2_out, nand_4_out);
  and and_19 (and_19_out, nor_2_out, nor_1_out, nand_3_out, A2);
  and and_20 (and_20_out, nor_1_out, nand_2_out, A3);
  and and_21 (and_21_out, nand_1_out, A4);
  nor nor_5 (YGT, and_9_out, and_10_out, and_11_out, and_12_out, and_13_out, and_14_out);
  nor nor_6 (YLT, and_16_out, and_17_out, and_18_out, and_19_out, and_20_out, and_21_out);
endmodule

// 7486
module DIP_7486 (
  input  A1,
  input  B1,
  input  A2,
  input  B2,
  input  A3,
  input  B3,
  input  A4,
  input  B4,
  output Y1,
  output Y2,
  output Y3,
  output Y4
);

  xor xor_1 (Y1, A1, B1);
  xor xor_2 (Y2, A2, B2);
  xor xor_3 (Y3, A3, B3);
  xor xor_4 (Y4, A4, B4);
endmodule

// 7495
module DIP_7495 (
  input  P0,
  input  P1,
  input  P2,
  input  P3,
  input  S,
  input  Data,
  input  CLK1,
  input  CLK2,
  output Q0,
  output Q1,
  output Q2,
  output Q3
);

  wire and_1_out, and_2_out, and_3_out, and_4_out, and_5_out, and_6_out, and_7_out, and_8_out, and_9_out,
       and_10_out, nor_1_out, nor_2_out, nor_3_out, nor_4_out, not_1_out, not_2_out, not_3_out, not_4_out,
       not_5_out, not_6_out, or_1_out;

  not not_1 (not_1_out, S);
  not not_2 (not_2_out, not_1_out);
  and and_1 (and_1_out, not_1_out, CLK1);
  and and_2 (and_2_out, S, CLK2);
  or or_1 (or_1_out, and_1_out, and_2_out);
  and and_3 (and_3_out, Data, not_1_out);
  nor nor_1 (nor_1_out, and_3_out, and_4_out);
  not not_3 (not_3_out, nor_1_out);
  and and_4 (and_4_out, not_2_out, P0);
  SR_Flip_Flop sr_flip_flop_1 (.CLK(or_1_out), .R(nor_1_out), .S(not_3_out), .Q1(Q0));  // open: CLR, SET, Q0
  and and_5 (and_5_out, Q0, not_1_out);
  nor nor_2 (nor_2_out, and_5_out, and_6_out);
  not not_4 (not_4_out, nor_2_out);
  and and_6 (and_6_out, not_2_out, P1);
  SR_Flip_Flop sr_flip_flop_2 (.CLK(or_1_out), .R(nor_2_out), .S(not_4_out), .Q1(Q1));  // open: CLR, SET, Q0
  and and_7 (and_7_out, Q1, not_1_out);
  nor nor_3 (nor_3_out, and_7_out, and_8_out);
  not not_5 (not_5_out, nor_3_out);
  and and_8 (and_8_out, not_2_out, P2);
  SR_Flip_Flop sr_flip_flop_3 (.CLK(or_1_out), .R(nor_3_out), .S(not_5_out), .Q1(Q2));  // open: CLR, SET, Q0
  and and_9 (and_9_out, Q2, not_1_out);
  and and_10 (and_10_out, not_2_out, P3);
  nor nor_4 (nor_4_out, and_9_out, and_10_out);
  not not_6 (not_6_out, nor_4_out);
  SR_Flip_Flop sr_flip_flop_4 (.CLK(or_1_out), .R(nor_4_out), .S(not_6_out), .Q1(Q3));  // open: CLR, SET, Q0
endmodule

// 74109
module DIP_74109 (
  input  SET1,
  input  J1,
  input  CLK1,
  input  K1,
  input  CLR1,
  input  SET2,
  input  J2,
  input  CLK2,
  input  K2,
  input  CLR2,
  output Q1,
  output R1,
  output Q2,
  output R2
);

  wire not_1_out, not_2_out, not_3_out, not_4_out, not_5_out, not_6_out;

  not not_1 (not_1_out, SET1);
  not not_2 (not_2_out, K1);
  not not_3 (not_3_out, CLR1);
  not not_4 (not_4_out, SET2);
  not not_5 (not_5_out, K2);
  not not_6 (not_6_out, CLR2);
  JK_Flip_Flop jk_flip_flop_1 (.CLR(not_3_out), .SET(not_1_out), .CLK(CLK1), .K(not_2_out), .J(J1), .R(R1), .Q(Q1));
  JK_Flip_Flop jk_flip_flop_2 (.CLR(not_6_out), .SET(not_4_out), .CLK(CLK2), .K(not_5_out), .J(J2), .R(R2), .Q(Q2));
endmodule

// 74138
module DIP_74138 (
  input  A0,
  input  A1,
  input  A2,
  input  OE1,
  input  in_5,
  input  OE2,
  output Y0,
  output Y1,
  output Y2,
  output Y3,
  output Y4,
  output Y5,
  output Y6,
  output Y7
);

  wire and_1_out, and_2_out, and_3_out, and_4_out, and_5_out, and_6_out, and_7_out, and_8_out, and_9_out,
       not_1_out, not_2_out, not_3_out, not_4_out, not_5_out;

  not not_1 (not_1_out, A0);
  not not_2 (not_2_out, A1);
  not not_3 (not_3_out, A2);
  not not_4 (not_4_out, OE1);
  not not_5 (not_5_out, in_5);
  and and_1 (and_1_out, not_4_out, not_5_out, OE2);
  and and_2 (and_2_out, not_1_out, not_2_out, not_3_out, and_1_out);
  not not_6 (Y0, and_2_out);
  and and_3 (and_3_out, A0, not_2_out, not_3_out, and_1_out);
  not not_7 (Y1, and_3_out);
  and and_4 (and_4_out, not_1_out, A1, not_3_out, and_1_out);
  not not_8 (Y2, and_4_out);
  and and_5 (and_5_out, A0, A1, not_3_out, and_1_out);
  not not_9 (Y3, and_5_out);
  and and_6 (and_6_out, not_1_out, not_2_out, A2, and_1_out);
  not not_10 (Y4, and_6_out);
  and and_7 (and_7_out, A0, not_2_out, A2, and_1_out);
  not not_11 (Y5, and_7_out);
  and and_8 (and_8_out, not_1_out, A1, A2, and_1_out);
  not not_12 (Y6, and_8_out);
  and and_9 (and_9_out, A0, A1, A2, and_1_out);
  not not_13 (Y7, and_9_out);
endmodule

// 74139
module DIP_74139 (
  input  A0,
  input  A1,
  input  OEA,
  input  B0,
  input  B1,
  input  OEB,
  output Y0,
  output Y1,
  output Y2,
  output Y3,
  output Z0,
  output Z1,
  output Z2,
  output Z3
);

  wire and_1_out, and_2_out, and_3_out, and_4_out, and_5_out, and_6_out, and_7_out, and_8_out, not_1_out,
       not_2_out, not_3_out, not_4_out, not_5_out, not_6_out;

  not not_1 (not_1_out, A0);
  not not_2 (not_2_out, A1);
  not not_3 (not_3_out, OEA);
  not not_4 (not_4_out, B0);
  not not_5 (not_5_out, B1);
  not not_6 (not_6_out, OEB);
  and and_1 (and_1_out, not_1_out, not_2_out, not_3_out);
  and and_2 (and_2_out, A0, not_2_out, not_3_out);
  and and_3 (and_3_out, not_1_out, A1, not_3_out);
  and and_4 (and_4_out, A0, A1, not_3_out);
  and and_5 (and_5_out, not_4_out, not_5_out, not_6_out);
  and and_6 (and_6_out, B0, not_5_out, not_6_out);
  and and_7 (and_7_out, not_4_out, B1, not_6_out);
  and and_8 (and_8_out, B0, B1, not_6_out);
  not not_7 (Y0, and_1_out);
  not not_8 (Y1, and_2_out);
  not not_9 (Y2, and_3_out);
  not not_10 (Y3, and_4_out);
  not not_11 (Z0, and_5_out);
  not not_12 (Z1, and_6_out);
  not not_13 (Z2, and_7_out);
  not not_14 (Z3, and_8_out);
endmodule

// 74147
module DIP_74147 (
  input  D1,
  input  D2,
  input  D3,
  input  D4,
  input  D5,
  input  D6,
  input  D7,
  input  D8,
  input  D9,
  output Y1,
  output Y2,
  output Y3,
  output Y4
);

  wire and_1_out, and_2_out, and_3_out, and_4_out, and_5_out, and_6_out, and_7_out, and_8_out, and_9_out,
       and_10_out, and_11_out, and_12_out, buffer_1_out, nor_1_out, not_1_out, not_2_out, not_3_out,
       not_4_out, not_5_out, not_6_out, not_7_out, not_8_out, not_9_out, not_10_out, not_11_out, not_12_out,
       not_13_out;

  not not_1 (not_1_out, D1);
  not not_2 (not_2_out, D2);
  not not_3 (not_3_out, D3);
  not not_4 (not_4_out, D4);
  not not_5 (not_5_out, D5);
  not not_6 (not_6_out, D6);
  not not_7 (not_7_out, D7);
  not not_8 (not_8_out, D8);
  not not_9 (not_9_out, D9);
  not not_10 (not_10_out, not_2_out);
  not not_11 (not_11_out, not_4_out);
  not not_12 (not_12_out, not_5_out);
  not not_13 (not_13_out, not_6_out);
  nor nor_1 (nor_1_out, not_8_out, not_9_out);
  and and_1 (and_1_out, not_10_out, not_13_out);
  and and_2 (and_2_out, not_3_out, not_11_out, not_13_out, nor_1_out);
  and and_3 (and_3_out, not_5_out, not_13_out, nor_1_out);
  and and_4 (and_4_out, not_7_out, nor_1_out);
  buf buffer_1 (buffer_1_out, not_9_out);
  and and_5 (and_5_out, not_2_out, not_11_out, not_12_out, nor_1_out);
  and and_6 (and_6_out, not_3_out, not_11_out, not_12_out, nor_1_out);
  and and_7 (and_7_out, not_6_out, nor_1_out);
  and and_8 (and_8_out, not_7_out, nor_1_out);
  and and_9 (and_9_out, not_4_out, nor_1_out);
  and and_10 (and_10_out, not_5_out, nor_1_out);
  and and_11 (and_11_out, not_6_out, nor_1_out);
  and and_12 (and_12_out, not_7_out, nor_1_out);
  nor nor_2 (Y1, and_2_out, and_4_out);
  nor nor_3 (Y2, and_5_out, and_6_out, and_7_out, and_8_out);
  nor nor_4 (Y3, and_9_out, and_10_out, and_11_out, and_12_out);
  nor nor_5 (Y4, not_8_out, not_9_out);
endmodule

// 74151
module DIP_74151 (
  input  S0,
  input  S1,
  input  S2,
  input  OE,
  input  A,
  input  B,
  input  C,
  input  D,
  input  E,
  input  F,
  input  G,
  input  J,
  output Y,
  output Z
);

  wire and_1_out, and_2_out, and_3_out, and_4_out, and_5_out, and_6_out, and_7_out, and_8_out, not_1_out,
       not_2_out, not_3_out, not_4_out;

  not not_1 (not_1_out, S2);
  not not_2 (not_2_out, OE);
  not not_3 (not_3_out, S1);
  not not_4 (not_4_out, S0);
  and and_1 (and_1_out, not_2_out, not_3_out);
  and and_2 (and_2_out, not_2_out, not_3_out);
  and and_3 (and_3_out, not_2_out, S1);
  and and_4 (and_4_out, not_2_out, S1);
  and and_5 (and_5_out, not_2_out, not_3_out);
  and and_6 (and_6_out, not_2_out, not_3_out);
  and and_7 (and_7_out, not_2_out, S1);
  and and_8 (and_8_out, not_2_out, S1);
  or or_1 (Y, and_1_out, and_2_out, and_3_out, and_4_out, and_5_out, and_6_out, and_7_out, and_8_out);
  not not_5 (Z, Y);
endmodule

// 74153
module DIP_74153 (
  input  S0,
  input  S1,
  input  OE1,
  input  A1,
  input  B1,
  input  C1,
  input  D1,
  input  OE2,
  input  A2,
  input  B2,
  input  C2,
  input  D2,
  output Y1,
  output Y2
);

  wire and_1_out, and_2_out, and_3_out, and_4_out, and_5_out, and_6_out, and_7_out, and_8_out, not_1_out,
       not_2_out, not_3_out, not_4_out;

  not not_1 (not_1_out, S1);
  not not_2 (not_2_out, OE1);
  not not_3 (not_3_out, OE2);
  not not_4 (not_4_out, S0);
  and and_1 (and_1_out, A1, not_2_out, not_4_out, not_1_out);
  and and_2 (and_2_out, B1, not_2_out, S0, not_1_out);
  and and_3 (and_3_out, C1, not_2_out, not_4_out, S1);
  and and_4 (and_4_out, D1, not_2_out, S0, S1);
  and and_5 (and_5_out, A2, not_3_out, not_4_out, not_1_out);
  and and_6 (and_6_out, B2, not_3_out, S0, not_1_out);
  and and_7 (and_7_out, C2, not_3_out, not_4_out, S1);
  and and_8 (and_8_out, D2, not_3_out, S0, S1);
  or or_1 (Y1, and_1_out, and_2_out, and_3_out, and_4_out);
  or or_2 (Y2, and_5_out, and_6_out, and_7_out, and_8_out);
endmodule

// 74157
module DIP_74157 (
  input  A1,
  input  B1,
  input  A2,
  input  B2,
  input  A3,
  input  B3,
  input  A4,
  input  B4,
  input  S0,
  input  OE,
  output Y1,
  output Y2,
  output Y3,
  output Y4
);

  wire and_1_out, and_2_out, and_3_out, and_4_out, and_5_out, and_6_out, and_7_out, and_8_out, not_1_out,
       not_2_out;

  not not_1 (not_1_out, S0);
  not not_2 (not_2_out, OE);
  and and_1 (and_1_out, A1, not_1_out, not_2_out);
  and and_2 (and_2_out, B1, S0, not_2_out);
  and and_3 (and_3_out, A2, not_1_out, not_2_out);
  and and_4 (and_4_out, B2, S0, not_2_out);
  and and_5 (and_5_out, A3, not_1_out, not_2_out);
  and and_6 (and_6_out, B3, S0, not_2_out);
  and and_7 (and_7_out, A4, not_1_out, not_2_out);
  and and_8 (and_8_out, B4, S0, not_2_out);
  or or_1 (Y1, and_1_out, and_2_out);
  or or_2 (Y2, and_3_out, and_4_out);
  or or_3 (Y3, and_5_out, and_6_out);
  or or_4 (Y4, and_7_out, and_8_out);
endmodule

// 74161
module DIP_74161 (
  input  CLK,
  input  CLR,
  input  LE,
  input  CEP,
  input  CET,
  input  D1,
  input  D2,
  input  D3,
  input  D4,
  output Q1,
  output Q2,
  output Q3,
  output Q4,
  output TC
);

  wire and_1_out, and_2_out, and_3_out, and_4_out, and_5_out, and_6_out, and_7_out, and_8_out, and_9_out,
       and_10_out, and_11_out, and_12_out, not_1_out, not_2_out, not_3_out, or_1_out, or_2_out, or_3_out,
       or_4_out, xor_1_out, xor_2_out, xor_3_out, xor_4_out;

  not not_1 (not_1_out, CLK);
  not not_2 (not_2_out, CLR);
  and and_1 (and_1_out, LE, CEP, CET);
  not not_3 (not_3_out, LE);
  and and_2 (and_2_out, D1, not_3_out);
  and and_3 (and_3_out, Q1, LE);
  and and_4 (and_4_out, D2, not_3_out);
  and and_5 (and_5_out, Q2, LE);
  and and_6 (and_6_out, Q1, and_1_out);
  and and_7 (and_7_out, D3, not_3_out);
  and and_8 (and_8_out, Q3, LE);
  and and_9 (and_9_out, Q2, Q1, and_1_out);
  and and_10 (and_10_out, D4, not_3_out);
  and and_11 (and_11_out, Q4, LE);
  and and_12 (and_12_out, Q3, Q2, Q1, and_1_out);
  xor xor_1 (xor_1_out, and_3_out, and_1_out);
  xor xor_2 (xor_2_out, and_5_out, and_6_out);
  xor xor_3 (xor_3_out, and_8_out, and_9_out);
  xor xor_4 (xor_4_out, and_11_out, and_12_out);
  or or_1 (or_1_out, and_2_out, xor_1_out);
  or or_2 (or_2_out, and_4_out, xor_2_out);
  or or_3 (or_3_out, and_7_out, xor_3_out);
  or or_4 (or_4_out, and_10_out, xor_4_out);
  D_Flip_Flop d_flip_flop_1 (.CLR(not_2_out), .D(or_1_out), .CLK(not_1_out), .Q(Q1));  // open: SET, R
  D_Flip_Flop d_flip_flop_2 (.CLR(not_2_out), .D(or_2_out), .CLK(not_1_out), .Q(Q2));  // open: SET, R
  D_Flip_Flop d_flip_flop_3 (.CLR(not_2_out), .D(or_3_out), .CLK(not_1_out), .Q(Q3));  // open: SET, R
  D_Flip_Flop d_flip_flop_4 (.CLR(not_2_out), .D(or_4_out), .CLK(not_1_out), .Q(Q4));  // open: SET, R
  and and_13 (TC, Q3, Q1);
endmodule

// 74163
module DIP_74163 (
  input  CLK,
  input  CE,
  input  LE,
  input  CEP,
  input  CET,
  input  D1,
  input  D2,
  input  D3,
  input  D4,
  output Q1,
  output Q2,
  output Q3,
  output Q4,
  output TC
);

  wire and_1_out, and_2_out, and_3_out, and_4_out, and_5_out, and_6_out, and_7_out, and_8_out, and_9_out,
       and_10_out, and_11_out, and_12_out, and_13_out, not_1_out, not_2_out, not_3_out, or_1_out, or_2_out,
       or_3_out, or_4_out, xor_1_out, xor_2_out, xor_3_out, xor_4_out;

  not not_1 (not_1_out, CLK);
  not not_2 (not_2_out, CE);
  and and_1 (and_1_out, LE, CEP, CET);
  not not_3 (not_3_out, LE);
  and and_2 (and_2_out, D1, not_2_out, not_3_out);
  and and_3 (and_3_out, Q1, not_2_out, LE);
  and and_4 (and_4_out, not_2_out, and_1_out);
  and and_5 (and_5_out, D2, not_2_out, not_3_out);
  and and_6 (and_6_out, Q2, not_2_out, LE);
  and and_7 (and_7_out, Q1, not_2_out, and_1_out);
  and and_8 (and_8_out, D3, not_2_out, not_3_out);
  and and_9 (and_9_out, Q3, not_2_out, LE);
  and and_10 (and_10_out, Q2, Q1, and_1_out, not_2_out);
  and and_11 (and_11_out, D4, not_2_out, not_3_out);
  and and_12 (and_12_out, Q4, not_2_out, LE);
  and and_13 (and_13_out, Q2, Q1);
  xor xor_1 (xor_1_out, and_3_out, and_4_out);
  xor xor_2 (xor_2_out, and_6_out, and_7_out);
  xor xor_3 (xor_3_out, and_9_out, and_10_out);
  xor xor_4 (xor_4_out, and_12_out, and_13_out);
  or or_1 (or_1_out, and_2_out, xor_1_out);
  or or_2 (or_2_out, and_5_out, xor_2_out);
  or or_3 (or_3_out, and_8_out, xor_3_out);
  or or_4 (or_4_out, and_11_out, xor_4_out);
  D_Flip_Flop d_flip_flop_1 (.D(or_1_out), .CLK(not_1_out), .Q(Q1));  // open: SET, CLR, R
  D_Flip_Flop d_flip_flop_2 (.D(or_2_out), .CLK(not_1_out), .Q(Q2));  // open: SET, CLR, R
  D_Flip_Flop d_flip_flop_3 (.D(or_3_out), .CLK(not_1_out), .Q(Q3));  // open: SET, CLR, R
  D_Flip_Flop d_flip_flop_4 (.D(or_4_out), .CLK(not_1_out), .Q(Q4));  // open: SET, CLR, R
  and and_14 (TC, Q3, Q1);
endmodule

// 74181
module DIP_74181 (
  input  S1,
  input  S2,
  input  S3,
  input  S4,
  input  B4,
  input  A4,
  input  B3,
  input  A3,
  input  B2,
  input  A2,
  input  B1,
  input  A1,
  input  M,
  input  CIN,
  output G,
  output COUT,
  output P,
  output Y4,
  output Y3,
  output EQ,
  output Y2,
  output Y1
);

  wire and_1_out, and_2_out, and_3_out, and_4_out, and_5_out, and_6_out, and_7_out, and_8_out, and_9_out,
       and_10_out, and_11_out, and_12_out, and_13_out, and_14_out, and_15_out, and_16_out, and_17_out,
       and_18_out, and_19_out, and_20_out, and_21_out, and_22_out, and_23_out, and_24_out, and_25_out,
       and_26_out, and_27_out, and_28_out, buffer_1_out, buffer_2_out, buffer_3_out, buffer_4_out,
       buffer_5_out, nand_1_out, nand_3_out, nor_1_out, nor_2_out, nor_3_out, nor_4_out, nor_5_out,
       nor_6_out, nor_7_out, nor_8_out, nor_10_out, nor_11_out, nor_12_out, not_1_out, not_2_out, not_3_out,
       not_4_out, not_5_out, xor_1_out, xor_2_out, xor_3_out, xor_4_out;

  not not_1 (not_1_out, B4);
  not not_2 (not_2_out, B3);
  not not_3 (not_3_out, B2);
  not not_4 (not_4_out, B1);
  not not_5 (not_5_out, M);
  and and_1 (and_1_out, B4, S1, A4);
  and and_2 (and_2_out, A4, S2, not_1_out);
  and and_3 (and_3_out, not_1_out, S3);
  and and_4 (and_4_out, S4, B4);
  buf buffer_1 (buffer_1_out, A4);
  and and_5 (and_5_out, B3, S1, A3);
  and and_6 (and_6_out, A3, S2, not_2_out);
  and and_7 (and_7_out, not_2_out, S3);
  and and_8 (and_8_out, S4, B3);
  buf buffer_2 (buffer_2_out, A3);
  and and_9 (and_9_out, B2, S1, A2);
  and and_10 (and_10_out, A2, S2, not_3_out);
  and and_11 (and_11_out, not_3_out, S3);
  and and_12 (and_12_out, S4, B2);
  buf buffer_3 (buffer_3_out, A2);
  and and_13 (and_13_out, B1, S1, A1);
  and and_14 (and_14_out, A1, S2, not_4_out);
  and and_15 (and_15_out, not_4_out, S3);
  and and_16 (and_16_out, S4, B1);
  buf buffer_4 (buffer_4_out, A1);
  nor nor_1 (nor_1_out, and_1_out, and_2_out);
  nor nor_2 (nor_2_out, and_3_out, and_4_out, buffer_1_out);
  nor nor_3 (nor_3_out, and_5_out, and_6_out);
  nor nor_4 (nor_4_out, and_7_out, and_8_out, buffer_2_out);
  nor nor_5 (nor_5_out, and_9_out, and_10_out);
  nor nor_6 (nor_6_out, and_11_out, and_12_out, buffer_3_out);
  nor nor_7 (nor_7_out, and_13_out, and_14_out);
  nor nor_8 (nor_8_out, and_15_out, and_16_out, buffer_4_out);
  xor xor_1 (xor_1_out, nor_1_out, nor_2_out);
  xor xor_2 (xor_2_out, nor_3_out, nor_4_out);
  xor xor_3 (xor_3_out, nor_5_out, nor_6_out);
  xor xor_4 (xor_4_out, nor_7_out, nor_8_out);
  buf buffer_5 (buffer_5_out, nor_2_out);
  and and_17 (and_17_out, nor_1_out, nor_4_out);
  and and_18 (and_18_out, nor_1_out, nor_3_out, nor_6_out);
  and and_19 (and_19_out, nor_1_out, nor_3_out, nor_5_out, nor_8_out);
  nand nand_1 (nand_1_out, nor_3_out, nor_7_out);
  nand nand_2 (P, nor_1_out, nor_3_out, nor_5_out, nor_7_out);
  and and_20 (and_20_out, nor_7_out, nor_3_out);
  and and_21 (and_21_out, nor_5_out, nor_3_out, nor_8_out, not_5_out);
  and and_22 (and_22_out, nor_3_out, nor_6_out, not_5_out);
  and and_23 (and_23_out, nor_4_out, not_5_out);
  and and_24 (and_24_out, CIN, nor_7_out, nor_5_out, not_5_out);
  and and_25 (and_25_out, nor_5_out, nor_8_out, not_5_out);
  and and_26 (and_26_out, nor_6_out, not_5_out);
  and and_27 (and_27_out, CIN, nor_7_out, not_5_out);
  and and_28 (and_28_out, nor_8_out, not_5_out);
  nand nand_3 (nand_3_out, CIN, not_5_out);
  nor nor_9 (G, buffer_5_out, and_17_out, and_18_out, and_19_out);
  nor nor_10 (nor_10_out, and_20_out, and_21_out, and_22_out, and_23_out);
  nor nor_11 (nor_11_out, and_24_out, and_25_out, and_26_out);
  nor nor_12 (nor_12_out, and_27_out, and_28_out);
  nor nor_13 (COUT, G, nand_1_out);
  xor xor_5 (Y4, xor_1_out, nor_10_out);
  xor xor_6 (Y3, xor_2_out, nor_11_out);
  xor xor_7 (Y2, xor_3_out, nor_12_out);
  xor xor_8 (Y1, xor_4_out, nand_3_out);
  and and_29 (EQ, Y3, Y4, Y1, Y2);
endmodule

// 74238
module DIP_74238 (
  input  A0,
  input  A1,
  input  A2,
  input  OE1,
  input  OE2,
  input  in_6,
  output Y0,
  output Y1,
  output Y2,
  output Y3,
  output Y4,
  output Y5,
  output Y6,
  output Y7
);

  wire and_1_out, not_1_out, not_2_out, not_3_out, not_4_out, not_5_out;

  not not_1 (not_1_out, A0);
  not not_2 (not_2_out, A1);
  not not_3 (not_3_out, A2);
  not not_4 (not_4_out, OE1);
  not not_5 (not_5_out, OE2);
  and and_1 (and_1_out, not_4_out, not_5_out, in_6);
  and and_2 (Y0, not_1_out, not_2_out, not_3_out, and_1_out);
  and and_3 (Y1, A0, not_2_out, not_3_out, and_1_out);
  and and_4 (Y2, not_1_out, A1, not_3_out, and_1_out);
  and and_5 (Y3, A0, A1, not_3_out, and_1_out);
  and and_6 (Y4, not_1_out, not_2_out, A2, and_1_out);
  and and_7 (Y5, A0, not_2_out, A2, and_1_out);
  and and_8 (Y6, not_1_out, A1, A2, and_1_out);
  and and_9 (Y7, A0, A1, A2, and_1_out);
endmodule

// 74244
module DIP_74244 (
  input  A1,
  input  A2,
  input  A3,
  input  A4,
  input  OEA,
  input  B1,
  input  B2,
  input  B3,
  input  B4,
  input  OEB,
  output Y1,
  output Y2,
  output Y3,
  output Y4,
  output Z1,
  output Z2,
  output Z3,
  output Z4
);

  wire not_1_out, not_2_out;

  not not_1 (not_1_out, OEA);
  not not_2 (not_2_out, OEB);
  assign Y1 = not_1_out ? A1 : 1'bz;  // Controlled_Buffer controlled_buffer_1
  assign Y2 = not_1_out ? A2 : 1'bz;  // Controlled_Buffer controlled_buffer_2
  assign Y3 = not_1_out ? A3 : 1'bz;  // Controlled_Buffer controlled_buffer_3
  assign Y4 = not_1_out ? A4 : 1'bz;  // Controlled_Buffer controlled_buffer_4
  assign Z1 = not_2_out ? B1 : 1'bz;  // Controlled_Buffer controlled_buffer_5
  assign Z2 = not_2_out ? B2 : 1'bz;  // Controlled_Buffer controlled_buffer_6
  assign Z3 = not_2_out ? B3 : 1'bz;  // Controlled_Buffer controlled_buffer_7
  assign Z4 = not_2_out ? B4 : 1'bz;  // Controlled_Buffer controlled_buffer_8
endmodule

// 74247
module DIP_74247 (
  input  LT,
  input  D1,
  input  D2,
  input  D3,
  input  D4,
  input  RBI,
  input  BI,
  output Ya,
  output Yb,
  output Yc,
  output Yd,
  output Ye,
  output Yf,
  output Qg
);

  wire and_1_out, and_2_out, and_3_out, and_4_out, and_5_out, and_6_out, and_7_out, and_8_out, and_9_out,
       and_10_out, and_11_out, and_12_out, and_13_out, and_14_out, and_15_out, and_16_out, and_17_out,
       buffer_1_out, buffer_2_out, nand_1_out, nand_2_out, nand_3_out, nand_4_out, nand_5_out, nand_6_out,
       nand_7_out, nand_8_out, nor_1_out, nor_2_out, nor_3_out, nor_4_out, nor_5_out, nor_6_out, nor_7_out,
       not_1_out, not_2_out;

  buf buffer_1 (buffer_1_out, LT);
  not not_1 (not_1_out, RBI);
  nand nand_1 (nand_1_out, not_1_out, buffer_1_out, not_2_out, nand_5_out, nand_4_out, nand_3_out);
  nand nand_2 (nand_2_out, nand_1_out, not_2_out);
  nand nand_3 (nand_3_out, D1, buffer_1_out);
  nand nand_4 (nand_4_out, D2, buffer_1_out);
  nand nand_5 (nand_5_out, D3, buffer_1_out);
  not not_2 (not_2_out, D4);
  nand nand_6 (nand_6_out, nand_1_out, nand_5_out);
  nand nand_7 (nand_7_out, nand_1_out, nand_4_out);
  nand nand_8 (nand_8_out, nand_1_out, nand_3_out);
  and and_1 (and_1_out, nand_7_out, nand_2_out);
  and and_2 (and_2_out, nand_3_out, nand_4_out, nand_6_out);
  and and_3 (and_3_out, nand_8_out, nand_4_out, nand_5_out, not_2_out);
  and and_4 (and_4_out, nand_7_out, nand_2_out);
  and and_5 (and_5_out, nand_8_out, nand_4_out, nand_6_out);
  and and_6 (and_6_out, nand_3_out, nand_7_out, nand_6_out);
  and and_7 (and_7_out, nand_6_out, nand_2_out);
  and and_8 (and_8_out, nand_3_out, nand_7_out, nand_5_out);
  and and_9 (and_9_out, nand_8_out, nand_4_out, nand_5_out, not_2_out);
  and and_10 (and_10_out, nand_3_out, nand_4_out, nand_6_out);
  and and_11 (and_11_out, nand_8_out, nand_7_out, nand_6_out);
  buf buffer_2 (buffer_2_out, nand_8_out);
  and and_12 (and_12_out, nand_4_out, nand_6_out);
  and and_13 (and_13_out, nand_8_out, nand_7_out);
  and and_14 (and_14_out, nand_7_out, nand_5_out);
  and and_15 (and_15_out, nand_8_out, nand_5_out, not_2_out);
  and and_16 (and_16_out, nand_8_out, nand_7_out, nand_6_out);
  and and_17 (and_17_out, nand_4_out, nand_5_out, not_2_out, buffer_1_out);
  nor nor_1 (nor_1_out, and_1_out, and_2_out, and_3_out);
  nor nor_2 (nor_2_out, and_4_out, and_5_out, and_6_out);
  nor nor_3 (nor_3_out, and_7_out, and_8_out);
  nor nor_4 (nor_4_out, and_9_out, and_10_out, and_11_out);
  nor nor_5 (nor_5_out, buffer_2_out, and_12_out);
  nor nor_6 (nor_6_out, and_13_out, and_14_out, and_15_out);
  nor nor_7 (nor_7_out, and_16_out, and_17_out);
  not not_3 (Ya, nor_1_out);
  not not_4 (Yb, nor_2_out);
  not not_5 (Yc, nor_3_out);
  not not_6 (Yd, nor_4_out);
  not not_7 (Ye, nor_5_out);
  not not_8 (Yf, nor_6_out);
  not not_9 (Qg, nor_7_out);
endmodule

// 74266
module DIP_74266 (
  input  A1,
  input  B1,
  input  A2,
  input  B2,
  input  A3,
  input  B3,
  input  A4,
  input  B4,
  output Y1,
  output Y2,
  output Y3,
  output Y4
);

  wire xnor_1_out, xnor_2_out, xnor_3_out, xnor_4_out;

  xnor xnor_1 (xnor_1_out, A1, B1);
  xnor xnor_2 (xnor_2_out, A2, B2);
  xnor xnor_3 (xnor_3_out, A3, B3);
  xnor xnor_4 (xnor_4_out, A4, B4);
  Transistor #(.\type ("n")) transistor_1 (.in(1'b0), .out(Y1), .gate(xnor_1_out));
  Transistor #(.\type ("n")) transistor_2 (.in(1'b0), .out(Y2), .gate(xnor_2_out));
  Transistor #(.\type ("n")) transistor_3 (.in(1'b0), .out(Y3), .gate(xnor_3_out));
  Transistor #(.\type ("n")) transistor_4 (.in(1'b0), .out(Y4), .gate(xnor_4_out));

  // Notes on the sheet:
  //   Y2: pull=down
  //   Y3: pull=down
  //   Y4: pull=down
  //   Y1: pull=down
endmodule

// 74273
module DIP_74273 (
  input  CLR,
  input  CLK,
  input  D1,
  input  D2,
  input  D3,
  input  D4,
  input  D5,
  input  D6,
  input  D7,
  input  D8,
  output Y1,
  output Y2,
  output Y3,
  output Y4,
  output Y5,
  output Y6,
  output Y7,
  output Y8
);

  wire not_1_out;

  not not_1 (not_1_out, CLR);
  D_Flip_Flop d_flip_flop_1 (.CLR(not_1_out), .D(D1), .CLK(CLK), .Q(Y1));  // open: SET, R
  D_Flip_Flop d_flip_flop_2 (.CLR(not_1_out), .D(D2), .CLK(CLK), .Q(Y2));  // open: SET, R
  D_Flip_Flop d_flip_flop_3 (.CLR(not_1_out), .D(D3), .CLK(CLK), .Q(Y3));  // open: SET, R
  D_Flip_Flop d_flip_flop_4 (.CLR(not_1_out), .D(D4), .CLK(CLK), .Q(Y4));  // open: SET, R
  D_Flip_Flop d_flip_flop_5 (.CLR(not_1_out), .D(D5), .CLK(CLK), .Q(Y5));  // open: SET, R
  D_Flip_Flop d_flip_flop_6 (.CLR(not_1_out), .D(D6), .CLK(CLK), .Q(Y6));  // open: SET, R
  D_Flip_Flop d_flip_flop_7 (.CLR(not_1_out), .D(D7), .CLK(CLK), .Q(Y7));  // open: SET, R
  D_Flip_Flop d_flip_flop_8 (.CLR(not_1_out), .D(D8), .CLK(CLK), .Q(Y8));  // open: SET, R
endmodule

// 74283
module DIP_74283 (
  input  CIN,
  input  A1,
  input  B1,
  input  A2,
  input  B2,
  input  A3,
  input  B3,
  input  A4,
  input  B4,
  output Y1,
  output Y2,
  output Y3,
  output Y4,
  output COUT
);

  wire and_1_out, and_2_out, and_3_out, and_4_out, and_5_out, and_6_out, and_7_out, and_8_out, and_9_out,
       and_10_out, and_11_out, and_12_out, and_13_out, and_14_out, nand_1_out, nand_2_out, nand_3_out,
       nand_4_out, nor_1_out, nor_2_out, nor_3_out, nor_4_out, nor_5_out, nor_6_out, nor_7_out, not_1_out,
       not_2_out, not_3_out, not_4_out, not_5_out, not_6_out;

  not not_1 (not_1_out, CIN);
  nor nor_1 (nor_1_out, A1, B1);
  nand nand_1 (nand_1_out, A1, B1);
  nor nor_2 (nor_2_out, A2, B2);
  nand nand_2 (nand_2_out, A2, B2);
  nor nor_3 (nor_3_out, A3, B3);
  nand nand_3 (nand_3_out, A3, B3);
  nor nor_4 (nor_4_out, A4, B4);
  nand nand_4 (nand_4_out, A4, B4);
  not not_2 (not_2_out, not_1_out);
  not not_3 (not_3_out, nor_1_out);
  and and_1 (and_1_out, not_1_out, nand_1_out);
  not not_4 (not_4_out, nor_2_out);
  and and_2 (and_2_out, not_1_out, nand_1_out, nand_2_out);
  and and_3 (and_3_out, nand_2_out, nor_1_out);
  not not_5 (not_5_out, nor_3_out);
  and and_4 (and_4_out, not_1_out, nand_1_out, nand_2_out, nand_3_out);
  and and_5 (and_5_out, nand_2_out, nand_3_out, nor_1_out);
  and and_6 (and_6_out, nand_3_out, nor_2_out);
  not not_6 (not_6_out, nor_4_out);
  and and_7 (and_7_out, nand_1_out, nand_3_out);
  and and_8 (and_8_out, nand_2_out, nand_3_out, nand_4_out, nor_1_out);
  and and_9 (and_9_out, nand_3_out, nand_4_out, nor_2_out);
  and and_10 (and_10_out, nand_4_out, nor_3_out);
  and and_11 (and_11_out, not_3_out, nand_1_out);
  nor nor_5 (nor_5_out, and_1_out, nor_1_out);
  and and_12 (and_12_out, not_4_out, nand_2_out);
  nor nor_6 (nor_6_out, and_2_out, and_3_out, nor_2_out);
  and and_13 (and_13_out, not_5_out, nand_3_out);
  nor nor_7 (nor_7_out, and_4_out, and_5_out, and_6_out, nor_3_out);
  and and_14 (and_14_out, not_6_out, nand_4_out);
  nor nor_8 (COUT, and_7_out, and_8_out, and_9_out, and_10_out, nor_4_out);
  xor xor_1 (Y1, not_2_out, and_11_out);
  xor xor_2 (Y2, nor_5_out, and_12_out);
  xor xor_3 (Y3, nor_6_out, and_13_out);
  xor xor_4 (Y4, nor_7_out, and_14_out);
endmodule

// 74373
module DIP_74373 (
  input  OE,
  input  LE,
  input  D1,
  input  D2,
  input  D3,
  input  D4,
  input  D5,
  input  D6,
  input  D7,
  input  D8,
  output Q1,
  output Q2,
  output Q3,
  output Q4,
  output Q5,
  output Q6,
  output Q7,
  output Q8
);

  wire d_latch_1_q, d_latch_2_q, d_latch_3_q, d_latch_4_q, d_latch_5_q, d_latch_6_q, d_latch_7_q,
       d_latch_8_q, not_1_out;

  not not_1 (not_1_out, OE);
  D_Latch d_latch_1 (.D(D1), .LE(LE), .Q(d_latch_1_q));  // open: SET, CLR, R
  D_Latch d_latch_2 (.D(D2), .LE(LE), .Q(d_latch_2_q));  // open: SET, CLR, R
  D_Latch d_latch_3 (.D(D3), .LE(LE), .Q(d_latch_3_q));  // open: SET, CLR, R
  D_Latch d_latch_4 (.D(D4), .LE(LE), .Q(d_latch_4_q));  // open: SET, CLR, R
  D_Latch d_latch_5 (.D(D5), .LE(LE), .Q(d_latch_5_q));  // open: SET, CLR, R
  D_Latch d_latch_6 (.D(D6), .LE(LE), .Q(d_latch_6_q));  // open: SET, CLR, R
  D_Latch d_latch_7 (.D(D7), .LE(LE), .Q(d_latch_7_q));  // open: SET, CLR, R
  D_Latch d_latch_8 (.D(D8), .LE(LE), .Q(d_latch_8_q));  // open: SET, CLR, R
  assign Q1 = not_1_out ? d_latch_1_q : 1'bz;  // Controlled_Buffer controlled_buffer_1
  assign Q2 = not_1_out ? d_latch_2_q : 1'bz;  // Controlled_Buffer controlled_buffer_2
  assign Q3 = not_1_out ? d_latch_3_q : 1'bz;  // Controlled_Buffer controlled_buffer_3
  assign Q4 = not_1_out ? d_latch_4_q : 1'bz;  // Controlled_Buffer controlled_buffer_4
  assign Q5 = not_1_out ? d_latch_5_q : 1'bz;  // Controlled_Buffer controlled_buffer_5
  assign Q6 = not_1_out ? d_latch_6_q : 1'bz;  // Controlled_Buffer controlled_buffer_6
  assign Q7 = not_1_out ? d_latch_7_q : 1'bz;  // Controlled_Buffer controlled_buffer_7
  assign Q8 = not_1_out ? d_latch_8_q : 1'bz;  // Controlled_Buffer controlled_buffer_8
endmodule

// 74374
module DIP_74374 (
  input  OE,
  input  CLK,
  input  D1,
  input  D2,
  input  D3,
  input  D4,
  input  D5,
  input  D6,
  input  D7,
  input  D8,
  output Q1,
  output Q2,
  output Q3,
  output Q4,
  output Q5,
  output Q6,
  output Q7,
  output Q8
);

  wire d_flip_flop_1_q, d_flip_flop_2_q, d_flip_flop_3_q, d_flip_flop_4_q, d_flip_flop_5_q, d_flip_flop_6_q,
       d_flip_flop_7_q, d_flip_flop_8_q, not_1_out;

  not not_1 (not_1_out, OE);
  D_Flip_Flop d_flip_flop_1 (.D(D1), .CLK(CLK), .Q(d_flip_flop_1_q));  // open: SET, CLR, R
  D_Flip_Flop d_flip_flop_2 (.D(D2), .CLK(CLK), .Q(d_flip_flop_2_q));  // open: SET, CLR, R
  D_Flip_Flop d_flip_flop_3 (.D(D3), .CLK(CLK), .Q(d_flip_flop_3_q));  // open: SET, CLR, R
  D_Flip_Flop d_flip_flop_4 (.D(D4), .CLK(CLK), .Q(d_flip_flop_4_q));  // open: SET, CLR, R
  D_Flip_Flop d_flip_flop_5 (.D(D5), .CLK(CLK), .Q(d_flip_flop_5_q));  // open: SET, CLR, R
  D_Flip_Flop d_flip_flop_6 (.D(D6), .CLK(CLK), .Q(d_flip_flop_6_q));  // open: SET, CLR, R
  D_Flip_Flop d_flip_flop_7 (.D(D7), .CLK(CLK), .Q(d_flip_flop_7_q));  // open: SET, CLR, R
  D_Flip_Flop d_flip_flop_8 (.D(D8), .CLK(CLK), .Q(d_flip_flop_8_q));  // open: SET, CLR, R
  assign Q1 = not_1_out ? d_flip_flop_1_q : 1'bz;  // Controlled_Buffer controlled_buffer_1
  assign Q2 = not_1_out ? d_flip_flop_2_q : 1'bz;  // Controlled_Buffer controlled_buffer_2
  assign Q3 = not_1_out ? d_flip_flop_3_q : 1'bz;  // Controlled_Buffer controlled_buffer_3
  assign Q4 = not_1_out ? d_flip_flop_4_q : 1'bz;  // Controlled_Buffer controlled_buffer_4
  assign Q5 = not_1_out ? d_flip_flop_5_q : 1'bz;  // Controlled_Buffer controlled_buffer_5
  assign Q6 = not_1_out ? d_flip_flop_6_q : 1'bz;  // Controlled_Buffer controlled_buffer_6
  assign Q7 = not_1_out ? d_flip_flop_7_q : 1'bz;  // Controlled_Buffer controlled_buffer_7
  assign Q8 = not_1_out ? d_flip_flop_8_q : 1'bz;  // Controlled_Buffer controlled_buffer_8
endmodule

// 74377
module DIP_74377 (
  input  CE,
  input  CLK,
  input  D1,
  input  D2,
  input  D3,
  input  D4,
  input  D5,
  input  D6,
  input  D7,
  input  D8,
  output Q1,
  output Q2,
  output Q3,
  output Q4,
  output Q5,
  output Q6,
  output Q7,
  output Q8
);

  wire and_1_out, not_1_out, not_2_out, or_1_out, or_2_out;

  not not_1 (not_1_out, CE);
  not not_2 (not_2_out, CLK);
  D_Flip_Flop d_flip_flop_1 (.D(D1), .CLK(and_1_out), .Q(Q1));  // open: SET, CLR, R
  D_Flip_Flop d_flip_flop_2 (.D(D2), .CLK(and_1_out), .Q(Q2));  // open: SET, CLR, R
  D_Flip_Flop d_flip_flop_3 (.D(D3), .CLK(and_1_out), .Q(Q3));  // open: SET, CLR, R
  D_Flip_Flop d_flip_flop_4 (.D(D4), .CLK(and_1_out), .Q(Q4));  // open: SET, CLR, R
  D_Flip_Flop d_flip_flop_5 (.D(D5), .CLK(and_1_out), .Q(Q5));  // open: SET, CLR, R
  D_Flip_Flop d_flip_flop_6 (.D(D6), .CLK(and_1_out), .Q(Q6));  // open: SET, CLR, R
  D_Flip_Flop d_flip_flop_7 (.D(D7), .CLK(and_1_out), .Q(Q7));  // open: SET, CLR, R
  D_Flip_Flop d_flip_flop_8 (.D(D8), .CLK(and_1_out), .Q(Q8));  // open: SET, CLR, R
  or or_1 (or_1_out, not_1_out, or_2_out);
  or or_2 (or_2_out, or_1_out, not_2_out);
  and and_1 (and_1_out, or_1_out, not_2_out);
endmodule

// 74573
module DIP_74573 (
  input  OE,
  input  LE,
  input  D1,
  input  D2,
  input  D3,
  input  D4,
  input  D5,
  input  D6,
  input  D7,
  input  D8,
  output Q1,
  output Q2,
  output Q3,
  output Q4,
  output Q5,
  output Q6,
  output Q7,
  output Q8
);

  wire d_latch_1_q, d_latch_2_q, d_latch_3_q, d_latch_4_q, d_latch_5_q, d_latch_6_q, d_latch_7_q,
       d_latch_8_q, not_1_out;

  not not_1 (not_1_out, OE);
  D_Latch d_latch_1 (.D(D1), .LE(LE), .Q(d_latch_1_q));  // open: SET, CLR, R
  D_Latch d_latch_2 (.D(D2), .LE(LE), .Q(d_latch_2_q));  // open: SET, CLR, R
  D_Latch d_latch_3 (.D(D3), .LE(LE), .Q(d_latch_3_q));  // open: SET, CLR, R
  D_Latch d_latch_4 (.D(D4), .LE(LE), .Q(d_latch_4_q));  // open: SET, CLR, R
  D_Latch d_latch_5 (.D(D5), .LE(LE), .Q(d_latch_5_q));  // open: SET, CLR, R
  D_Latch d_latch_6 (.D(D6), .LE(LE), .Q(d_latch_6_q));  // open: SET, CLR, R
  D_Latch d_latch_7 (.D(D7), .LE(LE), .Q(d_latch_7_q));  // open: SET, CLR, R
  D_Latch d_latch_8 (.D(D8), .LE(LE), .Q(d_latch_8_q));  // open: SET, CLR, R
  assign Q1 = not_1_out ? d_latch_1_q : 1'bz;  // Controlled_Buffer controlled_buffer_1
  assign Q2 = not_1_out ? d_latch_2_q : 1'bz;  // Controlled_Buffer controlled_buffer_2
  assign Q3 = not_1_out ? d_latch_3_q : 1'bz;  // Controlled_Buffer controlled_buffer_3
  assign Q4 = not_1_out ? d_latch_4_q : 1'bz;  // Controlled_Buffer controlled_buffer_4
  assign Q5 = not_1_out ? d_latch_5_q : 1'bz;  // Controlled_Buffer controlled_buffer_5
  assign Q6 = not_1_out ? d_latch_6_q : 1'bz;  // Controlled_Buffer controlled_buffer_6
  assign Q7 = not_1_out ? d_latch_7_q : 1'bz;  // Controlled_Buffer controlled_buffer_7
  assign Q8 = not_1_out ? d_latch_8_q : 1'bz;  // Controlled_Buffer controlled_buffer_8
endmodule

// 74574
module DIP_74574 (
  input  OE,
  input  CLK,
  input  D1,
  input  D2,
  input  D3,
  input  D4,
  input  D5,
  input  D6,
  input  D7,
  input  D8,
  output Q1,
  output Q2,
  output Q3,
  output Q4,
  output Q5,
  output Q6,
  output Q7,
  output Q8
);

  wire d_flip_flop_1_q, d_flip_flop_2_q, d_flip_flop_3_q, d_flip_flop_4_q, d_flip_flop_5_q, d_flip_flop_6_q,
       d_flip_flop_7_q, d_flip_flop_8_q, not_1_out;

  not not_1 (not_1_out, OE);
  D_Flip_Flop d_flip_flop_1 (.D(D1), .CLK(CLK), .Q(d_flip_flop_1_q));  // open: SET, CLR, R
  D_Flip_Flop d_flip_flop_2 (.D(D2), .CLK(CLK), .Q(d_flip_flop_2_q));  // open: SET, CLR, R
  D_Flip_Flop d_flip_flop_3 (.D(D3), .CLK(CLK), .Q(d_flip_flop_3_q));  // open: SET, CLR, R
  D_Flip_Flop d_flip_flop_4 (.D(D4), .CLK(CLK), .Q(d_flip_flop_4_q));  // open: SET, CLR, R
  D_Flip_Flop d_flip_flop_5 (.D(D5), .CLK(CLK), .Q(d_flip_flop_5_q));  // open: SET, CLR, R
  D_Flip_Flop d_flip_flop_6 (.D(D6), .CLK(CLK), .Q(d_flip_flop_6_q));  // open: SET, CLR, R
  D_Flip_Flop d_flip_flop_7 (.D(D7), .CLK(CLK), .Q(d_flip_flop_7_q));  // open: SET, CLR, R
  D_Flip_Flop d_flip_flop_8 (.D(D8), .CLK(CLK), .Q(d_flip_flop_8_q));  // open: SET, CLR, R
  assign Q1 = not_1_out ? d_flip_flop_1_q : 1'bz;  // Controlled_Buffer controlled_buffer_1
  assign Q2 = not_1_out ? d_flip_flop_2_q : 1'bz;  // Controlled_Buffer controlled_buffer_2
  assign Q3 = not_1_out ? d_flip_flop_3_q : 1'bz;  // Controlled_Buffer controlled_buffer_3
  assign Q4 = not_1_out ? d_flip_flop_4_q : 1'bz;  // Controlled_Buffer controlled_buffer_4
  assign Q5 = not_1_out ? d_flip_flop_5_q : 1'bz;  // Controlled_Buffer controlled_buffer_5
  assign Q6 = not_1_out ? d_flip_flop_6_q : 1'bz;  // Controlled_Buffer controlled_buffer_6
  assign Q7 = not_1_out ? d_flip_flop_7_q : 1'bz;  // Controlled_Buffer controlled_buffer_7
  assign Q8 = not_1_out ? d_flip_flop_8_q : 1'bz;  // Controlled_Buffer controlled_buffer_8
endmodule

// 74595
module DIP_74595 (
  input  OE,
  input  LCLK,
  input  D,
  input  SCLK,
  input  CLR,
  output Q1,
  output Q2,
  output Q3,
  output Q4,
  output Q5,
  output Q6,
  output Q7,
  output Q8,
  output Q8S
);

  wire d_flip_flop_1_q, d_flip_flop_2_q, d_flip_flop_3_q, d_flip_flop_4_q, d_flip_flop_5_q, d_flip_flop_6_q,
       d_flip_flop_7_q, d_flip_flop_9_q, d_flip_flop_10_q, d_flip_flop_11_q, d_flip_flop_12_q,
       d_flip_flop_13_q, d_flip_flop_14_q, d_flip_flop_15_q, d_flip_flop_16_q, not_1_out;

  not not_1 (not_1_out, OE);
  D_Flip_Flop d_flip_flop_1 (.CLR(CLR), .D(D), .CLK(SCLK), .Q(d_flip_flop_1_q));  // open: SET, R
  D_Flip_Flop d_flip_flop_2 (.CLR(CLR), .D(d_flip_flop_1_q), .CLK(SCLK), .Q(d_flip_flop_2_q));  // open: SET, R
  D_Flip_Flop d_flip_flop_3 (.CLR(CLR), .D(d_flip_flop_2_q), .CLK(SCLK), .Q(d_flip_flop_3_q));  // open: SET, R
  D_Flip_Flop d_flip_flop_4 (.CLR(CLR), .D(d_flip_flop_3_q), .CLK(SCLK), .Q(d_flip_flop_4_q));  // open: SET, R
  D_Flip_Flop d_flip_flop_5 (.CLR(CLR), .D(d_flip_flop_4_q), .CLK(SCLK), .Q(d_flip_flop_5_q));  // open: SET, R
  D_Flip_Flop d_flip_flop_6 (.CLR(CLR), .D(d_flip_flop_5_q), .CLK(SCLK), .Q(d_flip_flop_6_q));  // open: SET, R
  D_Flip_Flop d_flip_flop_7 (.CLR(CLR), .D(d_flip_flop_6_q), .CLK(SCLK), .Q(d_flip_flop_7_q));  // open: SET, R
  D_Flip_Flop d_flip_flop_8 (.CLR(CLR), .D(d_flip_flop_7_q), .CLK(SCLK), .Q(Q8S));  // open: SET, R
  D_Flip_Flop d_flip_flop_9 (.D(d_flip_flop_1_q), .CLK(LCLK), .Q(d_flip_flop_9_q));  // open: SET, CLR, R
  D_Flip_Flop d_flip_flop_10 (.D(d_flip_flop_2_q), .CLK(LCLK), .Q(d_flip_flop_10_q));  // open: SET, CLR, R
  D_Flip_Flop d_flip_flop_11 (.D(d_flip_flop_3_q), .CLK(LCLK), .Q(d_flip_flop_11_q));  // open: SET, CLR, R
  D_Flip_Flop d_flip_flop_12 (.D(d_flip_flop_4_q), .CLK(LCLK), .Q(d_flip_flop_12_q));  // open: SET, CLR, R
  D_Flip_Flop d_flip_flop_13 (.D(d_flip_flop_5_q), .CLK(LCLK), .Q(d_flip_flop_13_q));  // open: SET, CLR, R
  D_Flip_Flop d_flip_flop_14 (.D(d_flip_flop_6_q), .CLK(LCLK), .Q(d_flip_flop_14_q));  // open: SET, CLR, R
  D_Flip_Flop d_flip_flop_15 (.D(d_flip_flop_7_q), .CLK(LCLK), .Q(d_flip_flop_15_q));  // open: SET, CLR, R
  D_Flip_Flop d_flip_flop_16 (.D(Q8S), .CLK(LCLK), .Q(d_flip_flop_16_q));  // open: SET, CLR, R
  assign Q1 = not_1_out ? d_flip_flop_9_q : 1'bz;  // Controlled_Buffer controlled_buffer_1
  assign Q2 = not_1_out ? d_flip_flop_10_q : 1'bz;  // Controlled_Buffer controlled_buffer_2
  assign Q3 = not_1_out ? d_flip_flop_11_q : 1'bz;  // Controlled_Buffer controlled_buffer_3
  assign Q4 = not_1_out ? d_flip_flop_12_q : 1'bz;  // Controlled_Buffer controlled_buffer_4
  assign Q5 = not_1_out ? d_flip_flop_13_q : 1'bz;  // Controlled_Buffer controlled_buffer_5
  assign Q6 = not_1_out ? d_flip_flop_14_q : 1'bz;  // Controlled_Buffer controlled_buffer_6
  assign Q7 = not_1_out ? d_flip_flop_15_q : 1'bz;  // Controlled_Buffer controlled_buffer_7
  assign Q8 = not_1_out ? d_flip_flop_16_q : 1'bz;  // Controlled_Buffer controlled_buffer_8
endmodule

// 74670
module DIP_74670 (
  input  RE,
  input  RA,
  input  RB,
  input  WE,
  input  WA,
  input  WB,
  input  D1,
  input  D2,
  input  D3,
  input  D4,
  output Q1,
  output Q2,
  output Q3,
  output Q4
);

  wire and_1_out, and_2_out, and_3_out, and_4_out, and_5_out, and_6_out, and_7_out, and_8_out, and_9_out,
       and_10_out, and_11_out, and_12_out, and_13_out, and_14_out, and_15_out, and_16_out, and_17_out,
       and_18_out, and_19_out, and_20_out, and_21_out, and_22_out, d_ff_13_qn, d_ff_14_qn, d_ff_15_qn,
       nor_1_out, nor_2_out, nor_3_out, nor_4_out, not_1_out, not_2_out, not_3_out, not_4_out, not_5_out,
       not_6_out, not_7_out, not_8_out, not_9_out, not_10_out, not_11_out, not_12_out, not_13_out,
       not_14_out, undriven, undriven_2, undriven_3, undriven_4, undriven_5, undriven_6, undriven_7,
       undriven_8, undriven_9;

  not not_1 (not_1_out, RE);
  not not_2 (not_2_out, RA);
  not not_3 (not_3_out, RB);
  not not_4 (not_4_out, WE);
  not not_5 (not_5_out, WA);
  not not_6 (not_6_out, WB);
  and and_1 (and_1_out, not_6_out, and_2_out);
  not not_7 (not_7_out, D1);
  not not_8 (not_8_out, D2);
  not not_9 (not_9_out, D3);
  not not_10 (not_10_out, D4);
  not not_11 (not_11_out, not_6_out);
  and and_2 (and_2_out, not_5_out, not_4_out);
  and and_3 (and_3_out, and_2_out, not_11_out);
  D_Flip_Flop_part #(.trigger("high")) d_ff_1 (.preset(undriven), .reset(not_7_out));  // open: D, clk, Q, Qn
  D_Flip_Flop_part #(.trigger("high")) d_ff_2 (.preset(d_ff_13_qn), .reset(not_8_out));  // open: D, clk, Q, Qn
  D_Flip_Flop_part #(.trigger("high")) d_ff_3 (.preset(d_ff_14_qn), .reset(not_9_out));  // open: D, clk, Q, Qn
  D_Flip_Flop_part #(.trigger("high")) d_ff_4 (.preset(d_ff_15_qn), .reset(not_10_out));  // open: D, clk, Q, Qn
  not not_12 (not_12_out, not_5_out);
  and and_4 (and_4_out, not_6_out, and_5_out);
  D_Flip_Flop_part #(.trigger("high")) d_ff_5 (.preset(undriven_2), .reset(not_7_out));  // open: D, clk, Q, Qn
  D_Flip_Flop_part #(.trigger("high")) d_ff_6 (.preset(undriven_3), .reset(not_8_out));  // open: D, clk, Q, Qn
  D_Flip_Flop_part #(.trigger("high")) d_ff_7 (.preset(undriven_4), .reset(not_9_out));  // open: D, clk, Q, Qn
  D_Flip_Flop_part #(.trigger("high")) d_ff_8 (.preset(undriven_5), .reset(not_10_out));  // open: D, clk, Q, Qn
  and and_5 (and_5_out, not_12_out, not_4_out);
  and and_6 (and_6_out, and_5_out, not_11_out);
  D_Flip_Flop_part #(.trigger("high")) d_ff_9 (.preset(undriven_6), .reset(not_7_out));  // open: D, clk, Q, Qn
  D_Flip_Flop_part #(.trigger("high")) d_ff_10 (.preset(undriven_7), .reset(not_8_out));  // open: D, clk, Q, Qn
  D_Flip_Flop_part #(.trigger("high")) d_ff_11 (.preset(undriven_8), .reset(not_9_out));  // open: D, clk, Q, Qn
  D_Flip_Flop_part #(.trigger("high")) d_ff_12 (.preset(undriven_9), .reset(not_10_out));  // open: D, clk, Q, Qn
  not not_13 (not_13_out, not_3_out);
  D_Flip_Flop_part #(.trigger("high")) d_ff_13 (
    .clk(d_ff_13_qn), .Q(not_13_out), .Qn(d_ff_13_qn), .preset(not_13_out), .reset(not_13_out));  // open: D
  D_Flip_Flop_part #(.trigger("high")) d_ff_14 (
    .clk(d_ff_14_qn), .Q(not_13_out), .Qn(d_ff_14_qn), .preset(not_13_out), .reset(not_13_out));  // open: D
  D_Flip_Flop_part #(.trigger("high")) d_ff_15 (
    .clk(d_ff_15_qn), .Q(not_13_out), .Qn(d_ff_15_qn), .preset(not_13_out), .reset(not_13_out));  // open: D
  D_Flip_Flop_part #(.trigger("high")) d_ff_16 (.Q(not_13_out), .preset(not_13_out));  // open: D, clk, Qn, reset
  not not_14 (not_14_out, not_2_out);
  and and_7 (and_7_out, undriven, not_3_out, not_2_out);
  and and_8 (and_8_out, undriven_2, not_3_out, not_14_out);
  and and_9 (and_9_out, undriven_6, not_13_out, not_2_out);
  and and_10 (and_10_out, not_13_out, not_13_out, not_14_out);
  and and_11 (and_11_out, d_ff_13_qn, not_3_out, not_2_out);
  and and_12 (and_12_out, undriven_3, not_3_out, not_14_out);
  and and_13 (and_13_out, undriven_7, not_13_out, not_2_out);
  and and_14 (and_14_out, not_13_out, not_13_out, not_14_out);
  and and_15 (and_15_out, d_ff_14_qn, not_3_out, not_2_out);
  and and_16 (and_16_out, undriven_4, not_3_out, not_14_out);
  and and_17 (and_17_out, undriven_8, not_13_out, not_2_out);
  and and_18 (and_18_out, not_13_out, not_13_out, not_14_out);
  and and_19 (and_19_out, d_ff_15_qn, not_3_out, not_2_out);
  and and_20 (and_20_out, undriven_5, not_3_out, not_14_out);
  and and_21 (and_21_out, undriven_9, not_13_out, not_2_out);
  and and_22 (and_22_out, not_13_out, not_13_out, not_14_out);
  nor nor_1 (nor_1_out, and_7_out, and_8_out, and_9_out, and_10_out);
  assign Q1 = not_1_out ? nor_1_out : 1'bz;  // Controlled_Buffer controlled_buffer_1
  nor nor_2 (nor_2_out, and_11_out, and_12_out, and_13_out, and_14_out);
  assign Q2 = not_1_out ? nor_2_out : 1'bz;  // Controlled_Buffer controlled_buffer_2
  nor nor_3 (nor_3_out, and_15_out, and_16_out, and_17_out, and_18_out);
  assign Q3 = not_1_out ? nor_3_out : 1'bz;  // Controlled_Buffer controlled_buffer_3
  nor nor_4 (nor_4_out, and_19_out, and_20_out, and_21_out, and_22_out);
  assign Q4 = not_1_out ? nor_4_out : 1'bz;  // Controlled_Buffer controlled_buffer_4
endmodule

// 744049
module DIP_744049 (
  input  A1,
  input  A2,
  input  A3,
  input  A4,
  input  A5,
  input  A6,
  output Y1,
  output Y2,
  output Y3,
  output Y4,
  output Y5,
  output Y6
);

  not not_1 (Y1, A1);
  not not_2 (Y2, A2);
  not not_3 (Y3, A3);
  not not_4 (Y4, A4);
  not not_5 (Y5, A5);
  not not_6 (Y6, A6);
endmodule

// 744075
module DIP_744075 (
  input  A1,
  input  B1,
  input  C1,
  input  A2,
  input  B2,
  input  C2,
  input  A3,
  input  B3,
  input  C3,
  output Y1,
  output Y2,
  output Y3
);

  or or_1 (Y1, A1, B1, C1);
  or or_2 (Y2, A2, B2, C2);
  or or_3 (Y3, A3, B3, C3);
endmodule

// 744078
module DIP_744078 (
  input  A,
  input  B,
  input  C,
  input  D,
  input  E,
  input  F,
  input  G,
  input  H,
  output Y,
  output Z
);

  nor nor_1 (Y, A, B, C, D, E, F, G, H);
  not not_1 (Z, Y);
endmodule

// 744511
module DIP_744511 (
  input  LT,
  input  D1,
  input  D2,
  input  D3,
  input  D4,
  input  LE,
  input  BL,
  output Ya,
  output Yb,
  output Yc,
  output Yd,
  output Ye,
  output Yf,
  output Yg
);

  wire nand_1_out, nand_2_out, nand_3_out, nand_4_out, nand_5_out, nand_6_out, nand_7_out, nand_8_out,
       nand_9_out, nand_10_out, nand_11_out, nand_12_out, nand_13_out, nand_14_out, nand_15_out, nand_16_out,
       nand_17_out, nand_18_out, nand_19_out, nand_20_out, nand_21_out, nand_22_out, nand_23_out,
       nand_24_out, nand_25_out, nand_26_out, nand_27_out, nand_28_out, nand_29_out, nand_30_out,
       nand_31_out, nand_32_out, nand_33_out, nand_34_out, not_1_out, or_1_out;

  nand nand_1 (nand_1_out, D1, LE);
  nand nand_2 (nand_2_out, nand_1_out, nand_4_out);
  nand nand_3 (nand_3_out, nand_1_out, LE);
  nand nand_4 (nand_4_out, nand_2_out, nand_3_out);
  nand nand_5 (nand_5_out, D2, LE);
  nand nand_6 (nand_6_out, nand_5_out, nand_8_out);
  nand nand_7 (nand_7_out, nand_5_out, LE);
  nand nand_8 (nand_8_out, nand_6_out, nand_7_out);
  nand nand_9 (nand_9_out, D3, LE);
  nand nand_10 (nand_10_out, nand_9_out, nand_12_out);
  nand nand_11 (nand_11_out, nand_9_out, LE);
  nand nand_12 (nand_12_out, nand_10_out, nand_11_out);
  nand nand_13 (nand_13_out, D4, LE);
  nand nand_14 (nand_14_out, nand_13_out, nand_16_out);
  nand nand_15 (nand_15_out, nand_13_out, LE);
  nand nand_16 (nand_16_out, nand_14_out, nand_15_out);
  or or_1 (or_1_out, nand_6_out, nand_10_out);
  nand nand_17 (nand_17_out, nand_10_out, nand_6_out, nand_4_out);
  nand nand_18 (nand_18_out, nand_10_out, nand_2_out, nand_8_out);
  nand nand_19 (nand_19_out, nand_6_out, nand_4_out, nand_12_out);
  nand nand_20 (nand_20_out, nand_2_out, nand_12_out, nand_8_out);
  nand nand_21 (nand_21_out, nand_10_out, nand_8_out, nand_4_out);
  nand nand_22 (nand_22_out, nand_6_out, nand_12_out);
  nand nand_23 (nand_23_out, nand_16_out, nand_12_out, nand_8_out, nand_4_out);
  nand nand_24 (nand_24_out, nand_10_out, nand_6_out, nand_2_out);
  nand nand_25 (nand_25_out, nand_8_out, nand_12_out, nand_16_out, nand_2_out);
  nand nand_26 (nand_26_out, or_1_out, nand_14_out);
  nand nand_27 (nand_27_out, nand_26_out, BL);
  not not_1 (not_1_out, nand_27_out);
  nand nand_28 (nand_28_out, nand_17_out, not_1_out, nand_21_out, nand_25_out);
  nand nand_29 (nand_29_out, nand_18_out, nand_17_out, not_1_out);
  nand nand_30 (nand_30_out, nand_19_out, not_1_out);
  nand nand_31 (nand_31_out, nand_20_out, nand_21_out, not_1_out, nand_24_out);
  nand nand_32 (nand_32_out, nand_21_out, not_1_out, nand_4_out);
  nand nand_33 (nand_33_out, nand_22_out, not_1_out, nand_24_out, nand_25_out);
  nand nand_34 (nand_34_out, nand_23_out, nand_25_out, not_1_out, nand_24_out);
  nand nand_35 (Ya, nand_28_out, LT);
  nand nand_36 (Yb, nand_29_out, LT);
  nand nand_37 (Yc, nand_30_out, LT);
  nand nand_38 (Yd, nand_31_out, LT);
  nand nand_39 (Ye, nand_32_out, LT);
  nand nand_40 (Yf, nand_33_out, LT);
  nand nand_41 (Yg, nand_34_out, LT);
endmodule

module D_Latch (
  input  SET,
  input  D,
  input  LE,
  input  CLR,
  output Q,
  output R
);

  D_Flip_Flop_part #(.trigger("high")) d_ff_1 (.clk(LE), .D(D), .Q(CLR), .Qn(R), .preset(CLR), .reset(CLR));

  assign Q = CLR;
  assign SET = CLR;
endmodule

module D_Flip_Flop (
  input  SET,
  input  D,
  input  CLK,
  input  CLR,
  output Q,
  output R
);

  D_Flip_Flop_part d_ff_1 (.clk(CLK), .D(D), .Q(CLR), .Qn(R), .preset(CLR), .reset(CLR));

  assign Q = CLR;
  assign SET = CLR;
endmodule

module JK_Flip_Flop (
  input  SET,
  input  J,
  input  CLK,
  input  K,
  input  CLR,
  output Q,
  output R
);

  J_K_Flip_Flop j_k_ff_1 (.J(J), .clk(CLK), .K(K), .Q(Q), .Qn(R), .preset(SET), .reset(CLR));
endmodule

module SR_Flip_Flop (
  input  SET,
  input  S,
  input  CLK,
  input  R,
  input  CLR,
  output Q1,
  output Q0
);

  J_K_Flip_Flop j_k_ff_1 (.J(S), .clk(CLK), .K(R), .Q(Q1), .Qn(Q0), .preset(SET), .reset(CLR));
endmodule

module polarizedLED (
  input  GND,
  input  Vcc,
  output LED
);

  Transistor transistor_1 (.in(Vcc), .out(LED), .gate(GND));

  // Notes on the sheet:
  //   Vcc: pull=up
  //   GND: pull=up
  //   LED: pull=down
endmodule

// 74148
module DIP_74148 (
  input  D0,
  input  D1,
  input  D2,
  input  D3,
  input  D4,
  input  D5,
  input  D6,
  input  D7,
  input  EI,
  output EO,
  output GS,
  output A0,
  output A1,
  output A2
);

  wire and_1_out, and_2_out, and_3_out, and_4_out, and_5_out, and_6_out, and_7_out, and_8_out, and_9_out,
       and_10_out, and_11_out, and_12_out, not_1_out, not_2_out, not_3_out, not_4_out, not_5_out, not_6_out,
       not_7_out, not_8_out, not_9_out, not_10_out, not_11_out, not_12_out;

  not not_1 (not_1_out, D1);
  not not_2 (not_2_out, D2);
  not not_3 (not_3_out, D3);
  not not_4 (not_4_out, D4);
  not not_5 (not_5_out, D5);
  not not_6 (not_6_out, D6);
  not not_7 (not_7_out, D7);
  not not_8 (not_8_out, EI);
  not not_9 (not_9_out, not_2_out);
  not not_10 (not_10_out, not_4_out);
  not not_11 (not_11_out, not_5_out);
  not not_12 (not_12_out, not_6_out);
  nand nand_1 (EO, D0, D1, D2, D3, D4, D5, D6, D7, not_8_out);
  and and_1 (and_1_out, not_1_out, not_9_out, not_10_out, not_12_out, not_8_out);
  and and_2 (and_2_out, not_3_out, not_10_out, not_12_out, not_8_out);
  and and_3 (and_3_out, not_5_out, not_12_out, not_8_out);
  and and_4 (and_4_out, not_7_out, not_8_out);
  and and_5 (and_5_out, not_2_out, not_10_out, not_11_out, not_8_out);
  and and_6 (and_6_out, not_3_out, not_10_out, not_11_out, not_8_out);
  and and_7 (and_7_out, not_6_out, not_8_out);
  and and_8 (and_8_out, not_7_out, not_8_out);
  and and_9 (and_9_out, not_4_out, not_8_out);
  and and_10 (and_10_out, not_5_out, not_8_out);
  and and_11 (and_11_out, not_6_out, not_8_out);
  and and_12 (and_12_out, not_7_out, not_8_out);
  nand nand_2 (GS, EO, not_8_out);
  nor nor_1 (A0, and_1_out, and_2_out, and_3_out, and_4_out);
  nor nor_2 (A1, and_5_out, and_6_out, and_7_out, and_8_out);
  nor nor_3 (A2, and_9_out, and_10_out, and_11_out, and_12_out);
endmodule
